// Logisim project PB1204.circ as structural Verilog: 1 circuit, main circuit main
module main (
  input  [9:0] in_1,
  input  [3:0] DATAIN,
  output [3:0] DATAOUT,
  output [11:0] ADDRESS
);

  wire AddressRegister, AddressRegisterHigh, AddressRegisterLow, AddressRegisterMiddle, and_1_out, and_2_out,
       and_3_out, and_4_out, and_5_out, and_6_out, and_7_out, and_8_out, and_9_out, and_10_out, ARegister,
       BRegister, InstructionRegister, InterruptModeRegister, not_1_out, ProgramCounter, ProgramCounterHigh,
       ProgramCounterLow, ProgramCounterMiddle, pull_resistor_3_node, StackPointer, StackPointerRegisterHigh,
       StackPointerRegisterLow, StackPointerRegisterMiddle, UpdateInstReg;
  wire [3:0] ABuffer_q, ARegister_q, BBuffer_q, DATABUS, InstructionCounter_q, InstructionRegister_q,
       ProgramCounterHigh_q, ProgramCounterLow_q, ProgramCounterMiddle_q;
  wire [11:0] controlled_buffer_4_out, ProgramCounterRegister_q;

  and and_1 (and_1_out, ARegister, in_1[4]);
  and and_2 (and_2_out, ARegister, in_1[7]);
  and and_3 (and_3_out, ARegister, in_1[5]);
  and and_4 (and_4_out, in_1[4], BRegister);
  and and_5 (and_5_out, BRegister, in_1[7]);
  assign DATABUS = in_1[4] ? DATAIN : 4'bz;  // Controlled_Buffer controlled_buffer_1
  assign DATAOUT = not_1_out ? DATABUS : 4'bz;  // Controlled_Buffer controlled_buffer_2
  Pull_Resistor pull_resistor_1 (.node(in_1[4]));
  Pull_Resistor pull_resistor_2 (.node(DATABUS));
  not not_1 (not_1_out, in_1[4]);
  Register #(.width(4)) ABuffer (.D(DATABUS), .en(and_1_out), .clk(and_1_out), .Q(ABuffer_q));  // open: clr
  Register #(.width(4)) BBuffer (.D(DATABUS), .en(and_4_out), .clk(and_4_out), .Q(BBuffer_q));  // open: clr
  Register #(.width(4)) u_ARegister (.D(ABuffer_q), .en(and_2_out), .clk(and_2_out), .Q(ARegister_q));  // open: clr
  Register #(.width(4)) u_BRegister (.D(BBuffer_q), .en(and_5_out), .clk(and_5_out));  // open: Q, clr
  Counter #(.max('hf), .width(4)) InstructionCounter (.Q(InstructionCounter_q));  // open: clr, load, up, count, clk, D, carry
  assign DATABUS = and_3_out ? ARegister_q : 4'bz;  // Controlled_Buffer controlled_buffer_3
  Register #(.width(4)) u_InstructionRegister (
    .en(UpdateInstReg), .clk(UpdateInstReg), .Q(InstructionRegister_q), .clr(pull_resistor_3_node));  // open: D
  Pull_Resistor pull_resistor_3 (.node(pull_resistor_3_node));
  ROM #(.dataWidth(10)) rom_1 ();  // open: addr, data
  and and_6 (and_6_out, ProgramCounterLow, in_1[4]);
  and and_7 (and_7_out, ProgramCounterMiddle, in_1[4]);
  and and_8 (and_8_out, ProgramCounterHigh, in_1[4]);
  Register #(.width(4)) u_ProgramCounterLow (
    .D(DATABUS), .en(and_6_out), .clk(and_6_out), .Q(ProgramCounterLow_q));  // open: clr
  Register #(.width(4)) u_ProgramCounterMiddle (
    .D(DATABUS), .en(and_7_out), .clk(and_7_out), .Q(ProgramCounterMiddle_q));  // open: clr
  Register #(.width(4)) u_ProgramCounterHigh (
    .D(DATABUS), .en(and_8_out), .clk(and_8_out), .Q(ProgramCounterHigh_q));  // open: clr
  and and_9 (and_9_out, in_1[7], ProgramCounter);
  Demultiplexer #(.select(4)) demultiplexer_1 (
    .out0(InstructionRegister), .out1(InterruptModeRegister), .out2(AddressRegisterLow),
    .out3(AddressRegisterMiddle), .out4(AddressRegisterHigh), .out5(ProgramCounter), .out6(StackPointer),
    .out7(AddressRegister), .out8(ARegister), .out9(BRegister), .out10(ProgramCounterLow),
    .out11(ProgramCounterMiddle), .out12(ProgramCounterHigh), .out13(StackPointerRegisterLow),
    .out14(StackPointerRegisterMiddle), .out15(StackPointerRegisterHigh), .in(1'b1), .sel(in_1[3:0]));
  Counter #(.max('hfff), .width(12)) ProgramCounterRegister (
    .load(and_9_out), .clk(and_9_out),
    .D({ProgramCounterHigh_q, ProgramCounterMiddle_q, ProgramCounterLow_q}), .Q(ProgramCounterRegister_q));  // open: clr, up, count, carry
  assign controlled_buffer_4_out = and_10_out ? ProgramCounterRegister_q : 12'bz;  // Controlled_Buffer controlled_buffer_4
  and and_10 (and_10_out, AddressRegister, in_1[7]);
  Register #(.width(12)) u_AddressRegister (.D(controlled_buffer_4_out), .Q(ADDRESS));  // open: en, clk, clr
  Counter #(.max('hfff), .width(12)) StackPointerRegister ();  // open: clr, load, up, count, clk, D, carry, Q

  // Other names for the same wires on the sheet: ADDRESSBUS[11:0] = ADDRESS; ReadFromDatabus = in_1[4]; RW = in_1[4];
  //   WriteToDatabus = in_1[5]; ConnectToAddressBus = in_1[6]; TriggerUpdate = in_1[7]; IncrementRegister = in_1[8];
  //   DecrementRegister = in_1[9]
endmodule
