// Logisim project PB1204alu.circ as structural Verilog: 1 circuit, main circuit main
module main (
  input  NANDenable,
  input  NORenable,
  input  NOTenable,
  input  ADDenable,
  input  SLenable,
  input  SRenable,
  input  PRIMARYenable,
  input  SECONDARYenable,
  input  [3:0] PrimaryInput,
  input  [3:0] SecondaryInput,
  input  CarryIn,
  output [3:0] PrimaryOutput,
  output CarryOut,
  output BorrowOut
);

  wire adder_1_cout;
  wire [0:0] pull_resistor_1_node;
  wire [3:0] adder_1_out, nand_1_out, nor_1_out, not_1_out;
  wire [3:3] pull_resistor_2_node;

  Adder #(.width(4)) adder_1 (
    .a(PrimaryInput), .b(SecondaryInput), .out(adder_1_out), .cin(CarryIn), .cout(adder_1_cout));
  Pull_Resistor pull_resistor_1 (.node(pull_resistor_1_node[0]));
  Pull_Resistor pull_resistor_2 (.node(pull_resistor_2_node[3]));
  assign nand_1_out = ~(PrimaryInput & SecondaryInput);  // NAND_Gate nand_1, 4 bits wide
  assign PrimaryOutput = NANDenable ? nand_1_out : 4'bz;  // Controlled_Buffer controlled_buffer_1
  assign nor_1_out = ~(PrimaryInput | SecondaryInput);  // NOR_Gate nor_1, 4 bits wide
  assign PrimaryOutput = NORenable ? nor_1_out : 4'bz;  // Controlled_Buffer controlled_buffer_2
  assign not_1_out = ~PrimaryInput;  // NOT_Gate not_1, 4 bits wide
  or or_1 (CarryOut, adder_1_cout, PrimaryInput[3]);
  assign PrimaryOutput = NOTenable ? not_1_out : 4'bz;  // Controlled_Buffer controlled_buffer_3
  assign PrimaryOutput = ADDenable ? adder_1_out : 4'bz;  // Controlled_Buffer controlled_buffer_4
  assign PrimaryOutput = SLenable ? {PrimaryInput[2:0], pull_resistor_1_node[0]} : 4'bz;  // Controlled_Buffer controlled_buffer_5
  assign PrimaryOutput = SRenable ? {pull_resistor_2_node[3], PrimaryInput[3:1]} : 4'bz;  // Controlled_Buffer controlled_buffer_6
  Pull_Resistor pull_resistor_3 (.node(PrimaryOutput));
  assign PrimaryOutput = PRIMARYenable ? PrimaryInput : 4'bz;  // Controlled_Buffer controlled_buffer_7
  assign PrimaryOutput = SECONDARYenable ? SecondaryInput : 4'bz;  // Controlled_Buffer controlled_buffer_8

  assign BorrowOut = PrimaryInput[0];
endmodule
