// Logisim project PBP1204.circ as structural Verilog: 1 circuit, main circuit main
module main (
  input  ManualMode,
  input  [3:0] Action,
  input  [3:0] Location
);

  wire AAD, adder_1_cout, ANA, and_1_out, and_2_out, and_3_out, and_4_out, and_5_out, and_6_out, and_7_out,
       and_8_out, and_9_out, and_10_out, and_11_out, and_12_out, and_13_out, and_14_out, and_15_out,
       and_16_out, and_17_out, and_18_out, and_19_out, and_20_out, and_21_out, and_22_out, and_23_out,
       and_24_out, and_25_out, and_26_out, and_27_out, and_28_out, and_29_out, and_34_out, and_35_out,
       and_37_out, and_38_out, and_39_out, and_40_out, and_41_out, and_42_out, and_43_out, and_44_out,
       and_45_out, and_46_out, and_47_out, and_48_out, and_49_out, ANO, ANT, ARenable, ASL, ASR, BorrowFlag,
       BorrowFlagReset, BorrowFlagSet, BRenable, CarryFlag, CarryFlagReset, CarryFlagSet, CLK, clock_2_out,
       comparator_1_eq, CTF, CycleFinished, DEC, demultiplexer_2_out15, demultiplexer_3_out0,
       demultiplexer_3_out1, demultiplexer_3_out2, demultiplexer_3_out3, demultiplexer_3_out4,
       demultiplexer_3_out5, demultiplexer_3_out6, demultiplexer_3_out7, demultiplexer_4_out8,
       demultiplexer_4_out9, demultiplexer_4_out10, demultiplexer_4_out12, demultiplexer_4_out13,
       demultiplexer_4_out14, DirectFlagResult, EvenParityFlag, FlagResult, HBenable, HPCenable, HSPenable,
       INC, INTenable, IRenable, LBenable, LPCenable, LSPenable, MBenable, MPCenable, MSPenable, not_1_out,
       not_2_out, not_3_out, not_4_out, not_5_out, not_6_out, not_7_out, not_8_out, not_9_out, not_10_out,
       not_11_out, not_12_out, not_13_out, not_14_out, not_15_out, not_16_out, not_17_out, not_18_out,
       not_19_out, not_20_out, not_21_out, or_3_out, or_4_out, or_5_out, or_6_out, or_7_out, or_8_out,
       or_10_out, or_11_out, or_12_out, or_13_out, or_14_out, or_15_out, or_16_out, or_17_out, or_19_out,
       or_20_out, or_21_out, PCSPtick, pull_resistor_1_node, pull_resistor_3_node, pull_resistor_4_node,
       pull_resistor_9_node, pull_resistor_12_node, RBR, RDB, Read, RESET, RRD, RSenable, RSF, ShortWideInst,
       TFenable, UAR, WBR, WDB, xor_1_out, xor_2_out, xor_3_out, ZeroFlag;
  wire [3:0] ALUresult, AReg, BReg, controlled_buffer_4_out, controlled_buffer_4_out_2,
       controlled_buffer_13_out, controlled_buffer_35_out, DATA, HiBuffer, InstructionRegister_q, LowBuffer,
       MicrocodeLocation, MidBuffer, PreBufferConnection, ram_1_data, RegisterSelect, rom_1_data,
       TestFlagsRegister_q;
  wire [4:0] InstructionCounter_q;
  wire [7:0] Microcode_data;
  wire [11:0] ADDRESS, AddressBuffer, controlled_buffer_21_out, controlled_buffer_24_out,
       controlled_buffer_31_out, DirectOut, IncDecAddress, ProgramCounter, StackPointer;

  not not_1 (not_1_out, FlagResult);
  RAM #(.addrWidth(11), .asyncread("true"), .dataWidth(4), .databus("bidir"), .trigger("falling")) ram_1 (
    .addr(ADDRESS[10:0]), .we(WDB), .oe(Read), .clk(and_1_out), .data(ram_1_data));
  and and_1 (and_1_out, CLK, ADDRESS[11]);
  ROM #(.addrWidth(11), .dataWidth(4)) rom_1 (.addr(ADDRESS[10:0]), .data(rom_1_data));
  and and_2 (and_2_out, RRD, IRenable);
  and and_3 (and_3_out, LPCenable, RBR, not_1_out);
  POR por_1 (.out(RESET));
  Clock clock_1 (.out(CLK));
  or or_1 (Read, pull_resistor_1_node, RDB);
  or or_2 (CycleFinished, and_2_out, and_3_out, RESET);
  Pull_Resistor pull_resistor_1 (.node(pull_resistor_1_node));
  Pull_Resistor pull_resistor_2 (.node(DATA));
  Counter #(.max('h1f), .trigger("falling"), .width(5)) InstructionCounter (
    .clr(CycleFinished), .load(pull_resistor_3_node), .up(pull_resistor_4_node),
    .count(pull_resistor_4_node), .clk(CLK), .D({5{1'b0}}), .Q(InstructionCounter_q));  // open: carry
  Pull_Resistor pull_resistor_3 (.node(pull_resistor_3_node));
  Pull_Resistor #(.pull(1)) pull_resistor_4 (.node(pull_resistor_4_node));
  Pull_Resistor pull_resistor_5 (.node(ADDRESS));
  and and_4 (and_4_out, ADDRESS[11], Read);
  and and_5 (and_5_out, ADDRESS[11], WDB);
  assign DATA = and_4_out ? ram_1_data : 4'bz;  // Controlled_Buffer controlled_buffer_1
  assign ram_1_data = and_5_out ? DATA : 4'bz;  // Controlled_Buffer controlled_buffer_2
  and and_6 (and_6_out, not_2_out, Read);
  assign DATA = and_6_out ? rom_1_data : 4'bz;  // Controlled_Buffer controlled_buffer_3
  Register #(.trigger("falling"), .width(4)) InstructionRegister (
    .D(DATA), .en(IRenable), .clk(CLK), .Q(InstructionRegister_q), .clr(CycleFinished));
  not not_2 (not_2_out, ADDRESS[11]);
  Hex_Digit_Display #(.decimalPoint("false")) hex_digit_display_1 (.value(DATA));
  Hex_Digit_Display #(.decimalPoint("false")) hex_digit_display_2 (.value(AReg));
  Hex_Digit_Display #(.decimalPoint("false")) hex_digit_display_3 (.value(BReg));
  // Probe on {ShortWideInst, InstructionRegister_q, InstructionCounter_q}
  ROM #(.addrWidth(10)) Microcode (
    .addr({ShortWideInst, InstructionRegister_q, InstructionCounter_q}), .data(Microcode_data));
  Hex_Digit_Display #(.decimalPoint("false")) hex_digit_display_4 (.value(ADDRESS[11:8]));
  Hex_Digit_Display #(.decimalPoint("false")) hex_digit_display_5 (.value(ADDRESS[7:4]));
  Hex_Digit_Display #(.decimalPoint("false")) hex_digit_display_6 (.value(ProgramCounter[11:8]));
  Hex_Digit_Display #(.decimalPoint("false")) hex_digit_display_7 (.value(ProgramCounter[7:4]));
  Hex_Digit_Display #(.decimalPoint("false")) hex_digit_display_8 (.value(StackPointer[11:8]));
  Hex_Digit_Display #(.decimalPoint("false")) hex_digit_display_9 (.value(StackPointer[7:4]));
  Hex_Digit_Display #(.decimalPoint("false")) hex_digit_display_10 (.value(HiBuffer));
  Hex_Digit_Display #(.decimalPoint("false")) hex_digit_display_11 (.value(MidBuffer));
  Hex_Digit_Display #(.decimalPoint("false")) hex_digit_display_12 (.value(ADDRESS[3:0]));
  Hex_Digit_Display #(.decimalPoint("false")) hex_digit_display_13 (.value(ProgramCounter[3:0]));
  Hex_Digit_Display #(.decimalPoint("false")) hex_digit_display_14 (.value(StackPointer[3:0]));
  Hex_Digit_Display #(.decimalPoint("false")) hex_digit_display_15 (.value(LowBuffer));
  assign {controlled_buffer_4_out_2, controlled_buffer_4_out} = ManualMode ? {Location, Action} : 8'bz;  // Controlled_Buffer controlled_buffer_4
  not not_3 (not_3_out, ManualMode);
  assign {controlled_buffer_4_out_2, controlled_buffer_4_out} = not_3_out ? Microcode_data : 8'bz;  // Controlled_Buffer controlled_buffer_5
  not not_4 (not_4_out, RSF);
  and and_7 (and_7_out, not_4_out, CLK);
  Comparator #(.mode("unsigned"), .width(4)) comparator_1 (
    .a(controlled_buffer_4_out_2), .b(4'b1111), .eq(comparator_1_eq));  // open: gt, lt
  Demultiplexer #(.select(4)) demultiplexer_1 (
    .out0(RDB), .out1(WDB), .out2(RBR), .out3(WBR), .out4(RSF), .out5(UAR), .out6(CTF), .out7(RRD),
    .out8(ANA), .out9(ANO), .out10(ANT), .out11(AAD), .out12(ASL), .out13(ASR), .out14(INC), .out15(DEC),
    .in(CLK), .sel(controlled_buffer_4_out));
  Demultiplexer #(.select(4)) demultiplexer_2 (
    .out0(IRenable), .out1(LBenable), .out2(MBenable), .out3(HBenable), .out4(ARenable), .out5(BRenable),
    .out6(TFenable), .out7(RSenable), .out8(LPCenable), .out9(MPCenable), .out10(HPCenable),
    .out11(INTenable), .out12(LSPenable), .out13(MSPenable), .out14(HSPenable),
    .out15(demultiplexer_2_out15), .in(and_7_out), .sel(MicrocodeLocation));
  Pull_Resistor pull_resistor_6 (.node(MicrocodeLocation));
  assign MicrocodeLocation = not_5_out ? controlled_buffer_4_out_2 : 4'bz;  // Controlled_Buffer controlled_buffer_6
  not not_5 (not_5_out, comparator_1_eq);
  assign MicrocodeLocation = comparator_1_eq ? RegisterSelect : 4'bz;  // Controlled_Buffer controlled_buffer_7
  not not_6 (not_6_out, WDB);
  and and_8 (and_8_out, not_6_out, LBenable);
  Pull_Resistor pull_resistor_7 (.node(PreBufferConnection));
  assign PreBufferConnection = AAD ? ALUresult : 4'bz;  // Controlled_Buffer controlled_buffer_8
  assign PreBufferConnection = RDB ? DATA : 4'bz;  // Controlled_Buffer controlled_buffer_9
  and and_9 (and_9_out, ARenable, WBR);
  assign PreBufferConnection = and_9_out ? AReg : 4'bz;  // Controlled_Buffer controlled_buffer_10
  and and_10 (and_10_out, BRenable, WBR);
  assign PreBufferConnection = and_10_out ? BReg : 4'bz;  // Controlled_Buffer controlled_buffer_11
  not not_7 (not_7_out, WBR);
  or or_3 (or_3_out, INC, DEC);
  and and_11 (and_11_out, CLK, RSenable);
  or or_4 (or_4_out, and_10_out, and_8_out, and_9_out);
  and and_12 (and_12_out, not_7_out, TFenable);
  and and_13 (and_13_out, TFenable, RRD);
  or or_5 (or_5_out, and_13_out, RESET);
  or or_6 (or_6_out, RESET, CycleFinished);
  Counter #(.max('hf), .trigger("falling"), .width(4)) u_RegisterSelect (
    .clr(or_6_out), .load(not_8_out), .up(INC), .count(or_3_out), .clk(and_11_out), .D(DATA),
    .Q(RegisterSelect));  // open: carry
  not not_8 (not_8_out, or_3_out);
  and and_14 (and_14_out, LBenable, UAR);
  Register #(.trigger("falling"), .width(4)) u_LowBuffer (
    .D(PreBufferConnection), .en(or_4_out), .clk(CLK), .Q(LowBuffer), .clr(RESET));
  Register #(.trigger("falling"), .width(4)) u_MidBuffer (
    .D(PreBufferConnection), .en(MBenable), .clk(CLK), .Q(MidBuffer), .clr(RESET));
  Register #(.trigger("falling"), .width(4)) u_HiBuffer (
    .D(PreBufferConnection), .en(HBenable), .clk(CLK), .Q(HiBuffer), .clr(RESET));
  Register #(.trigger("falling"), .width(4)) TestFlagsRegister (
    .D(PreBufferConnection), .en(and_12_out), .clk(CLK), .Q(TestFlagsRegister_q), .clr(or_5_out));
  assign AddressBuffer[3:0] = INC ? BReg : 4'bz;  // Controlled_Buffer controlled_buffer_12
  or or_7 (or_7_out, and_14_out, RBR);
  or or_8 (or_8_out, RSF, or_12_out);
  assign controlled_buffer_13_out = RSF ? MicrocodeLocation : 4'bz;  // Controlled_Buffer controlled_buffer_13
  not not_9 (not_9_out, RSF);
  assign controlled_buffer_13_out = not_9_out ? TestFlagsRegister_q : 4'bz;  // Controlled_Buffer controlled_buffer_14
  assign AddressBuffer[3:0] = or_7_out ? LowBuffer : 4'bz;  // Controlled_Buffer controlled_buffer_15
  assign AddressBuffer[7:4] = or_7_out ? MidBuffer : 4'bz;  // Controlled_Buffer controlled_buffer_16
  assign AddressBuffer[11:8] = or_7_out ? HiBuffer : 4'bz;  // Controlled_Buffer controlled_buffer_17
  Demultiplexer #(.select(3)) demultiplexer_3 (
    .out0(demultiplexer_3_out0), .out1(demultiplexer_3_out1), .out2(demultiplexer_3_out2),
    .out3(demultiplexer_3_out3), .out4(demultiplexer_3_out4), .out5(demultiplexer_3_out5),
    .out6(demultiplexer_3_out6), .out7(demultiplexer_3_out7), .in(or_8_out),
    .sel(controlled_buffer_13_out[2:0]));
  assign DATA = and_17_out ? LowBuffer : 4'bz;  // Controlled_Buffer controlled_buffer_18
  assign DATA = and_16_out ? MidBuffer : 4'bz;  // Controlled_Buffer controlled_buffer_19
  assign DATA = and_15_out ? HiBuffer : 4'bz;  // Controlled_Buffer controlled_buffer_20
  not not_10 (not_10_out, BorrowFlag);
  not not_11 (not_11_out, EvenParityFlag);
  Demultiplexer #(.select(4)) demultiplexer_4 (
    .out8(demultiplexer_4_out8), .out9(demultiplexer_4_out9), .out10(demultiplexer_4_out10),
    .out12(demultiplexer_4_out12), .out13(demultiplexer_4_out13), .out14(demultiplexer_4_out14), .in(1'b1),
    .sel(RegisterSelect));  // open: out0, out1, out2, out3, out4, out5, out6, out7, out11, out15
  and and_15 (and_15_out, HBenable, WDB);
  and and_16 (and_16_out, MBenable, WDB);
  and and_17 (and_17_out, LBenable, WDB);
  not not_12 (not_12_out, ZeroFlag);
  not not_13 (not_13_out, CarryFlag);
  or or_9 (ShortWideInst, demultiplexer_4_out8, demultiplexer_4_out9, demultiplexer_4_out10, demultiplexer_4_out12, demultiplexer_4_out13, demultiplexer_4_out14);
  not not_14 (not_14_out, WBR);
  and and_18 (and_18_out, not_14_out, ARenable);
  and and_19 (and_19_out, ARenable, RRD);
  not not_15 (not_15_out, WBR);
  and and_20 (and_20_out, not_15_out, BRenable);
  and and_21 (and_21_out, BRenable, RRD);
  Pull_Resistor pull_resistor_8 (.node(AddressBuffer[3:0]));
  or or_10 (or_10_out, and_19_out, RESET);
  or or_11 (or_11_out, and_21_out, RESET);
  and and_22 (and_22_out, demultiplexer_3_out0, ZeroFlag);
  and and_23 (and_23_out, demultiplexer_3_out1, CarryFlag);
  and and_24 (and_24_out, demultiplexer_3_out2, BorrowFlag);
  and and_25 (and_25_out, demultiplexer_3_out3, EvenParityFlag);
  and and_26 (and_26_out, demultiplexer_3_out4, not_12_out);
  and and_27 (and_27_out, demultiplexer_3_out5, not_13_out);
  and and_28 (and_28_out, demultiplexer_3_out6, not_10_out);
  and and_29 (and_29_out, demultiplexer_3_out7, not_11_out);
  and and_30 (CarryFlagReset, demultiplexer_3_out1, RSF);
  and and_31 (CarryFlagSet, demultiplexer_3_out5, RSF);
  and and_32 (BorrowFlagReset, demultiplexer_3_out2, RSF);
  and and_33 (BorrowFlagSet, demultiplexer_3_out6, RSF);
  Register #(.trigger("falling"), .width(4)) ARegister (
    .D(AddressBuffer[3:0]), .en(and_18_out), .clk(CLK), .Q(AReg), .clr(or_10_out));
  Register #(.trigger("falling"), .width(4)) BRegister (
    .D(AddressBuffer[3:0]), .en(and_20_out), .clk(CLK), .Q(BReg), .clr(or_11_out));
  and and_34 (and_34_out, CTF, CLK);
  and and_35 (and_35_out, CLK, RSF);
  or or_12 (or_12_out, and_34_out, and_35_out);
  or or_13 (or_13_out, controlled_buffer_13_out[3], and_22_out, and_23_out, and_24_out, and_25_out, and_26_out, and_27_out, and_28_out, and_29_out);
  and and_36 (DirectFlagResult, or_12_out, or_13_out);
  and and_37 (and_37_out, CTF, CLK);
  not not_16 (not_16_out, and_47_out);
  or or_14 (or_14_out, RESET, CycleFinished);
  D_Flip_Flop #(.trigger("falling")) FlagTest (
    .D(DirectFlagResult), .clk(and_37_out), .Q(FlagResult), .preset(or_14_out));  // open: Qn, reset
  and and_38 (and_38_out, LSPenable, CTF, not_16_out);
  and and_39 (and_39_out, RBR, FlagResult);
  and and_40 (and_40_out, FlagResult, RBR);
  or or_15 (or_15_out, INC, and_38_out, DEC);
  or or_16 (or_16_out, PCSPtick, and_38_out);
  or or_17 (or_17_out, LPCenable, TFenable, LSPenable);
  assign controlled_buffer_21_out = and_40_out ? AddressBuffer : 12'bz;  // Controlled_Buffer controlled_buffer_21
  or or_18 (PCSPtick, and_40_out, or_15_out);
  assign controlled_buffer_21_out = or_15_out ? IncDecAddress : 12'bz;  // Controlled_Buffer controlled_buffer_22
  Controlled_Buffer #(.width(12)) controlled_buffer_23 (.in(controlled_buffer_21_out), .en(PCSPtick));  // open: out
  assign controlled_buffer_24_out = DEC ? IncDecAddress : 12'bz;  // Controlled_Buffer controlled_buffer_24
  assign controlled_buffer_24_out = INC ? IncDecAddress : 12'bz;  // Controlled_Buffer controlled_buffer_25
  and and_41 (and_41_out, or_17_out, and_39_out);
  assign controlled_buffer_24_out = and_41_out ? AddressBuffer : 12'bz;  // Controlled_Buffer controlled_buffer_26
  assign controlled_buffer_24_out = UAR ? DirectOut : 12'bz;  // Controlled_Buffer controlled_buffer_27
  Register #(.trigger("falling"), .width(12)) u_ProgramCounter (
    .D(controlled_buffer_21_out), .en(and_42_out), .clk(CLK), .Q(ProgramCounter), .clr(RESET));
  and and_42 (and_42_out, LPCenable, PCSPtick);
  and and_43 (and_43_out, or_16_out, LSPenable);
  not not_17 (not_17_out, CLK);
  or or_19 (or_19_out, DEC, INC, and_41_out, UAR);
  Register #(.trigger("falling"), .width(12)) AddressRegister (
    .D(controlled_buffer_24_out), .en(or_19_out), .clk(CLK), .Q(ADDRESS), .clr(RESET));
  Clock clock_2 (.out(clock_2_out));
  Pull_Resistor pull_resistor_9 (.node(pull_resistor_9_node));
  Adder #(.width(4)) adder_1 (.a(AReg), .b(BReg), .out(ALUresult), .cin(CarryFlag), .cout(adder_1_cout));
  D_Flip_Flop #(.trigger("falling")) u_CarryFlag (
    .D(adder_1_cout), .clk(and_44_out), .Q(CarryFlag), .preset(CarryFlagSet), .reset(or_20_out));  // open: Qn
  and and_44 (and_44_out, AAD, clock_2_out);
  WideRegisterWithSetReset wideregisterwithsetreset_1 (
    .WE(and_43_out), .CLK(not_17_out), .S(RESET), .DATA(controlled_buffer_21_out), .Q(StackPointer));  // open: R
  xor xor_1 (xor_1_out, AReg[3], pull_resistor_9_node);
  or or_20 (or_20_out, RESET, CarryFlagReset);
  assign DirectOut = LPCenable ? ProgramCounter : 12'bz;  // Controlled_Buffer controlled_buffer_28
  Pull_Resistor pull_resistor_10 (.node(StackPointer));
  assign DirectOut = LSPenable ? StackPointer : 12'bz;  // Controlled_Buffer controlled_buffer_29
  nor nor_1 (ZeroFlag, AReg[0], AReg[1], AReg[2], AReg[3]);
  xor xor_2 (xor_2_out, AReg[2], xor_1_out);
  D_Flip_Flop u_BorrowFlag (.Q(BorrowFlag));  // open: D, clk, Qn, preset, reset
  Pull_Resistor pull_resistor_11 (.node(DirectOut));
  assign DirectOut = TFenable ? ADDRESS : 12'bz;  // Controlled_Buffer controlled_buffer_30
  xor xor_3 (xor_3_out, AReg[1], xor_2_out);
  not not_18 (not_18_out, DirectFlagResult);
  not not_19 (not_19_out, DEC);
  and and_45 (and_45_out, DEC, DirectFlagResult);
  and and_46 (and_46_out, DEC, not_18_out);
  and and_47 (and_47_out, not_19_out, DirectFlagResult);
  assign controlled_buffer_31_out = and_46_out ? {12{1'b1}} : 12'bz;  // Controlled_Buffer controlled_buffer_31
  assign controlled_buffer_31_out = and_45_out ? 12'h3 : 12'bz;  // Controlled_Buffer controlled_buffer_32
  xor xor_4 (EvenParityFlag, AReg[0], xor_3_out);
  not not_20 (not_20_out, DEC);
  not not_21 (not_21_out, DirectFlagResult);
  and and_48 (and_48_out, not_20_out, not_21_out);
  assign controlled_buffer_31_out = and_48_out ? 12'h1 : 12'bz;  // Controlled_Buffer controlled_buffer_33
  assign controlled_buffer_31_out = and_47_out ? 12'hffd : 12'bz;  // Controlled_Buffer controlled_buffer_34
  Pull_Resistor pull_resistor_12 (.node(pull_resistor_12_node));
  Adder #(.width(12)) adder_2 (
    .a(DirectOut), .b(controlled_buffer_31_out), .out(IncDecAddress), .cin(pull_resistor_12_node));  // open: cout
  assign controlled_buffer_35_out = LPCenable ? ProgramCounter[3:0] : 4'bz;  // Controlled_Buffer controlled_buffer_35
  assign controlled_buffer_35_out = LSPenable ? StackPointer[3:0] : 4'bz;  // Controlled_Buffer controlled_buffer_36
  assign controlled_buffer_35_out = MPCenable ? ProgramCounter[7:4] : 4'bz;  // Controlled_Buffer controlled_buffer_37
  assign controlled_buffer_35_out = HPCenable ? ProgramCounter[11:8] : 4'bz;  // Controlled_Buffer controlled_buffer_38
  assign controlled_buffer_35_out = MSPenable ? StackPointer[7:4] : 4'bz;  // Controlled_Buffer controlled_buffer_39
  assign controlled_buffer_35_out = HSPenable ? StackPointer[11:8] : 4'bz;  // Controlled_Buffer controlled_buffer_40
  Pull_Resistor pull_resistor_13 (.node(controlled_buffer_35_out));
  assign DATA = and_49_out ? controlled_buffer_35_out : 4'bz;  // Controlled_Buffer controlled_buffer_41
  or or_21 (or_21_out, HPCenable, MPCenable, LPCenable, LSPenable, MSPenable, HSPenable);
  and and_49 (and_49_out, WDB, or_21_out);

  // Other names for the same wires on the sheet: Write = WDB

  // Notes on the sheet:
  //   contents of rom_1 (hex, n*v repeats v):
  //   0 5 1 0 4 0 5 5 0 1 0 0 8 6 0 0 b 3 4 4 5 6 8 0 8 7 1
  //   Microcode & Decode Section
  //   contents of Microcode (hex, n*v repeats v):
  //   0 8e 70 8e 10 f2 8e 7 25*0 8e 70 8e 10 8e 20 8e 30 62 f3 11 8e 7 19*0 8e 85 70 6e 10 6e 20 6e 30 62
  //   10 f2 8e 85 7 17*0 8e 70 f3 c5 11 cf 8e 7 12*0 7 11*0 8e 70 ce 10 f2 8e 7 25*0 8e 60 8e 10 8e 20 8e
  //   30 8e c5 a1 cf 91 cf 81 cf 86 82 7 13*0 8e 60 8e ce 10 ce 20 ce 30 c6 82 7 20*0 8e 60 8e 10 8e 20 8e
  //   30 8e 86 82 7 116*0 1b 42 8e 7 92*0 43 4e 52 8e 7 27*0 8e 70 f4 f4 8e 85 7 25*0 8e 70 8e 10 8e 20 8e
  //   30 f2 7 86*0 8e 70 c5 f1 7f cf f1 7f cf f1 cf 8e 7
  //   Location
  //   Action
  //   Buffer & Register Section
  //   Conditional Section
  //   Hack to make SWP work!
  //   Register Select Section
  //   Address Section
  //   Arrithmetic and Logic Unit
endmodule
