// Logisim project 12BitIncrementAndDecrementCounterWithLoadAndSetReset.circ as structural Verilog: 1 circuit, main circuit WideCounterWithSR
module WideCounterWithSR (
  input  LOAD,
  input  RESET,
  input  SET,
  input  UPDOWN,
  input  [11:0] DATA,
  input  CLK,
  input  NXTIN,
  output [11:0] DATAOUT,
  output NXTOUT
);

  wire nibbleincrementanddecrementcounterwithloadandsetreset_1_nxtout,
       nibbleincrementanddecrementcounterwithloadandsetreset_2_nxtout;

  NibbleIncrementAndDecrementCounterWithLoadAndSetReset nibbleincrementanddecrementcounterwithloadandsetreset_1 (
    .D(DATA[3:0]), .LOAD(LOAD), .RESET(RESET), .SET(SET), .UPDOWN(UPDOWN), .NXTIN(NXTIN), .CLK(CLK),
    .DATAOUT(DATAOUT[3:0]), .NXTOUT(nibbleincrementanddecrementcounterwithloadandsetreset_1_nxtout));
  NibbleIncrementAndDecrementCounterWithLoadAndSetReset nibbleincrementanddecrementcounterwithloadandsetreset_2 (
    .D(DATA[7:4]), .LOAD(LOAD), .RESET(RESET), .SET(SET), .UPDOWN(UPDOWN),
    .NXTIN(nibbleincrementanddecrementcounterwithloadandsetreset_1_nxtout), .CLK(CLK),
    .DATAOUT(DATAOUT[7:4]), .NXTOUT(nibbleincrementanddecrementcounterwithloadandsetreset_2_nxtout));
  NibbleIncrementAndDecrementCounterWithLoadAndSetReset nibbleincrementanddecrementcounterwithloadandsetreset_3 (
    .D(DATA[11:8]), .LOAD(LOAD), .RESET(RESET), .SET(SET), .UPDOWN(UPDOWN),
    .NXTIN(nibbleincrementanddecrementcounterwithloadandsetreset_2_nxtout), .CLK(CLK),
    .DATAOUT(DATAOUT[11:8]), .NXTOUT(NXTOUT));
endmodule
