// Logisim project 4BitIncrementAndDecrementCounterWithLoadAndSetReset.circ as structural Verilog: 1 circuit, main circuit NibbleIncrementAndDecrementCounterWithLoadAndSetReset
module NibbleIncrementAndDecrementCounterWithLoadAndSetReset (
  input  [3:0] D,
  input  LOAD,
  input  RESET,
  input  SET,
  input  UPDOWN,
  input  NXTIN,
  input  CLK,
  output [3:0] DATAOUT,
  output NXTOUT
);

  wire and_1_out, and_2_out, and_3_out, and_4_out, and_5_out, and_6_out, and_7_out, and_8_out, and_9_out,
       and_10_out, and_11_out, and_12_out, and_13_out, and_14_out, and_15_out, and_16_out, and_17_out,
       j_k_ff_1_qn, j_k_ff_2_qn, j_k_ff_3_qn, j_k_ff_4_qn, not_1_out, not_2_out, not_3_out, not_4_out,
       not_5_out, not_6_out, or_1_out, or_2_out, or_3_out, or_4_out, or_5_out, or_6_out, or_7_out, or_8_out,
       or_9_out, or_10_out, or_11_out;

  not not_1 (not_1_out, UPDOWN);
  and and_1 (and_1_out, LOAD, CLK);
  or or_1 (or_1_out, SET, and_2_out);
  J_K_Flip_Flop j_k_ff_1 (
    .J(NXTIN), .K(NXTIN), .clk(CLK), .Q(DATAOUT[0]), .Qn(j_k_ff_1_qn), .preset(or_1_out), .reset(or_2_out));
  not not_2 (not_2_out, not_1_out);
  not not_3 (not_3_out, D[0]);
  and and_2 (and_2_out, and_1_out, D[0]);
  and and_3 (and_3_out, and_1_out, not_3_out);
  or or_2 (or_2_out, RESET, and_3_out);
  and and_4 (and_4_out, not_1_out, DATAOUT[0]);
  and and_5 (and_5_out, j_k_ff_1_qn, not_2_out);
  or or_3 (or_3_out, SET, and_6_out);
  J_K_Flip_Flop j_k_ff_2 (
    .J(or_4_out), .K(or_4_out), .clk(CLK), .Q(DATAOUT[1]), .Qn(j_k_ff_2_qn), .preset(or_3_out),
    .reset(or_5_out));
  or or_4 (or_4_out, and_4_out, and_5_out);
  not not_4 (not_4_out, D[1]);
  and and_6 (and_6_out, and_1_out, D[1]);
  and and_7 (and_7_out, and_1_out, not_4_out);
  or or_5 (or_5_out, RESET, and_7_out);
  and and_8 (and_8_out, and_4_out, DATAOUT[1]);
  and and_9 (and_9_out, j_k_ff_2_qn, and_5_out);
  or or_6 (or_6_out, SET, and_10_out);
  J_K_Flip_Flop j_k_ff_3 (
    .J(or_7_out), .K(or_7_out), .clk(CLK), .Q(DATAOUT[2]), .Qn(j_k_ff_3_qn), .preset(or_6_out),
    .reset(or_8_out));
  or or_7 (or_7_out, and_8_out, and_9_out);
  not not_5 (not_5_out, D[2]);
  and and_10 (and_10_out, and_1_out, D[2]);
  and and_11 (and_11_out, and_1_out, not_5_out);
  or or_8 (or_8_out, RESET, and_11_out);
  and and_12 (and_12_out, and_8_out, DATAOUT[2]);
  and and_13 (and_13_out, j_k_ff_3_qn, and_9_out);
  or or_9 (or_9_out, SET, and_15_out);
  J_K_Flip_Flop j_k_ff_4 (
    .J(or_10_out), .K(or_10_out), .clk(CLK), .Q(DATAOUT[3]), .Qn(j_k_ff_4_qn), .preset(or_9_out),
    .reset(or_11_out));
  or or_10 (or_10_out, and_12_out, and_13_out);
  not not_6 (not_6_out, D[3]);
  and and_14 (and_14_out, and_1_out, not_6_out);
  and and_15 (and_15_out, and_1_out, D[3]);
  or or_11 (or_11_out, RESET, and_14_out);
  and and_16 (and_16_out, and_12_out, DATAOUT[3]);
  and and_17 (and_17_out, j_k_ff_4_qn, and_13_out);
  or or_12 (NXTOUT, and_16_out, and_17_out);
endmodule
